// Logisim project industrial_control_module_for_automated_assembly_line_pla_circuit.circ as structural Verilog: 1 circuit, main circuit main
module main (
  input  S4,
  input  S3,
  input  S2,
  input  S1,
  input  S0,
  output A0,
  output A1,
  output A2,
  output A3,
  output A4,
  output A5,
  output A6
);

  wire and_1_out, and_3_out, and_5_out, and_7_out, and_8_out, and_9_out, and_10_out, and_11_out, and_12_out,
       and_13_out, and_14_out, and_15_out, and_17_out, and_18_out, and_19_out, and_20_out, and_21_out,
       and_22_out, and_23_out, and_24_out, not_1_out, not_2_out, not_3_out, not_4_out, not_5_out;

  not not_1 (not_1_out, S3);
  not not_2 (not_2_out, S4);
  not not_3 (not_3_out, S2);
  not not_4 (not_4_out, S0);
  not not_5 (not_5_out, S1);
  and and_1 (and_1_out, not_2_out, not_1_out, not_3_out, not_5_out, not_4_out);
  // AND_Gate and_2 has open pins: in0=not_2_out, in1=not_1_out, in2=not_3_out, in3=not_5_out, in4=S0, out=open
  and and_3 (and_3_out, not_2_out, not_1_out, not_3_out, S1, not_4_out);
  // AND_Gate and_4 has open pins: in0=not_2_out, in1=not_1_out, in2=not_3_out, in3=S1, in4=S0, out=open
  and and_5 (and_5_out, not_2_out, not_1_out, S2, not_5_out, not_4_out);
  // AND_Gate and_6 has open pins: in0=not_2_out, in1=not_1_out, in2=S2, in3=not_5_out, in4=S0, out=open
  and and_7 (and_7_out, not_2_out, not_1_out, S2, S1, not_4_out);
  and and_8 (and_8_out, not_2_out, not_1_out, S2, S1, S0);
  and and_9 (and_9_out, not_2_out, S3, not_3_out, not_5_out, not_4_out);
  and and_10 (and_10_out, not_2_out, S3, not_3_out, not_5_out, S0);
  and and_11 (and_11_out, not_2_out, S3, not_3_out, S1, not_4_out);
  and and_12 (and_12_out, not_2_out, S3, not_3_out, S1, S0);
  and and_13 (and_13_out, not_2_out, S3, S2, not_5_out, not_4_out);
  and and_14 (and_14_out, not_2_out, S3, S2, not_5_out, S0);
  and and_15 (and_15_out, not_2_out, S3, S2, S1, not_4_out);
  // AND_Gate and_16 has open pins: in0=not_2_out, in1=S3, in2=S2, in3=S1, in4=S0, out=open
  and and_17 (and_17_out, S4, not_1_out, not_3_out, not_5_out, not_4_out);
  and and_18 (and_18_out, S4, not_1_out, not_3_out, not_5_out, S0);
  and and_19 (and_19_out, S4, not_1_out, not_3_out, S1, not_4_out);
  and and_20 (and_20_out, S4, not_1_out, not_3_out, S1, S0);
  and and_21 (and_21_out, S4, not_1_out, S2, not_5_out, not_4_out);
  and and_22 (and_22_out, S4, not_1_out, S2, not_5_out, S0);
  and and_23 (and_23_out, S4, not_1_out, S2, S1, not_4_out);
  and and_24 (and_24_out, S4, not_1_out, S2, S1, S0);
  and and_25 (and_24_out, S4, S3, not_3_out, not_5_out, not_4_out);
  and and_26 (and_24_out, S4, S3, not_3_out, not_5_out, S0);
  and and_27 (and_24_out, S4, S3, not_3_out, S1, not_4_out);
  and and_28 (and_24_out, S4, S3, not_3_out, S1, S0);
  and and_29 (and_24_out, S4, S3, S2, not_5_out, not_4_out);
  and and_30 (and_24_out, S4, S3, S2, not_5_out, S0);
  and and_31 (and_24_out, S4, S3, S2, S1, not_4_out);
  and and_32 (and_24_out, S4, S3, S2, S1, S0);
  or or_1 (A0, and_17_out, and_18_out, and_19_out, and_20_out, and_21_out, and_22_out, and_23_out, and_24_out, and_24_out, and_24_out, and_24_out, and_24_out, and_24_out, and_24_out, and_24_out, and_24_out);
  or or_2 (A1, and_8_out, and_9_out, and_10_out, and_11_out, and_12_out, and_13_out, and_14_out, and_15_out, and_24_out, and_24_out, and_24_out, and_24_out, and_24_out, and_24_out, and_24_out, and_24_out);
  or or_3 (A2, and_3_out, and_11_out, and_19_out, and_24_out);
  or or_4 (A3, and_7_out, and_15_out, and_23_out, and_24_out);
  or or_5 (A4, and_7_out, and_15_out, and_23_out, and_24_out);
  or or_6 (A5, and_1_out, and_3_out, and_5_out, and_7_out, and_9_out, and_11_out, and_13_out, and_15_out, and_17_out, and_19_out, and_21_out, and_23_out, and_24_out, and_24_out, and_24_out, and_24_out);
  or or_7 (A6, and_24_out, and_24_out);
endmodule
